# Fritzing sketch esp-now-mqtt-gateway (saved by Fritzing 0.9.5d)

parts:
  Composant1 = Ethernet W5500 [part_number=w5500]
  A2 = ESP32-S3-WROOM-1-N16R8 dev board

nets:
  N1: Composant1.GND, A2.Pin_44
  N2: Composant1.RST, A2.Pin_15
  N3: Composant1.3V3, A2.Pin_1
  N4: Composant1.MISO, A2.Pin_19
  N5: Composant1.MOSI, A2.Pin_17
  N6: Composant1.CS, A2.Pin_16
  N7: Composant1.SCK, A2.Pin_18
  N8: Composant1.INT, A2.Pin_8

custom parts:
  ESP32-S3-WROOM-1-N16R8 dev board: ESP32-S3 WIFI+BLE5.0 Development Board ESP32-S3-WROOM-1-N16R8(16M Flash/8SRAM).
